# Fritzing sketch hyperpan (saved by Fritzing 0.9.2b)

parts:
  GPIO = Raspberry Pi 2
  Theta = DRV8834 Low-Voltage Stepper Motor Driver Carrier [part_number="DRV 8834"]
  Phi = DRV8834 Low-Voltage Stepper Motor Driver Carrier [part_number="DRV 8834"]
  M3 = Stepper Motor - Bipolar
  J3 = male pin header, 4 pins [form="♂ (male)"]
  R3 = Resistor [tolerance=±5% resistance=330 package="0603 [SMD]"]
  led_4 = smd LED [color="Green (560nm)" package="1206 [SMD]"]
  J5 = single row smd female pin header, 4 pins [form="♀ (female)"]
  THETA = single row smd female pin header, 4 pins [form="♀ (female)"]
  R2 = Resistor [tolerance=±5% resistance=330 package="0603 [SMD]"]
  led_3 = smd LED [color="Green (560nm)" package="1206 [SMD]"]
  C1 = Electrolytic Capacitor [capacitance=100µF voltage=16V package="100 mil [THT, electrolytic]"]
  C2 = Electrolytic Capacitor [capacitance=100µF voltage=16V package="100 mil [THT, electrolytic]"]
  J6 = female pin header, 4 pins [form="♀ (female)"]
  M4 = Stepper Motor - Bipolar
  J4 = male pin header, 4 pins [form="♂ (male)"]
  5V_8A = Power plug
  Shutter1 = smd LED [color="Red (633nm)" package="1206 [SMD]"]
  Focus1 = smd LED [color="Green (560nm)" package="1206 [SMD]"]
  F_opto = TLP621 [package=THT]
  S_opto = TLP621 [package=THT]
  Trigger_Connector = female pin header, 3 pins [form="♀ (female)"]
  Alerts2 = smd LED [color="Red (633nm)" package="1206 [SMD]"]
  R6 = Resistor [tolerance=±5% resistance=330 package="0603 [SMD]"]

nets:
  N1: GPIO.GPIO4, F_opto.Pin_1
  N2: GPIO.GND, Theta.GND#147, led_4.cathode, Shutter1.cathode, Focus1.cathode, R6.Pin_0
  N3: GPIO.GPIO17, S_opto.Pin_1
  N4: GPIO.GPIO27, Theta.STEP
  N5: GPIO.GPIO22, Theta.SLEEP
  N6: GPIO.GPIO5, Phi.DIRECTION
  N7: GPIO.GPIO6, Phi.STEP
  N8: GPIO.GPIO13, Phi.M1
  N9: GPIO.GPIO21, Alerts2.anode
  N10: GPIO.GPIO16, Phi.M0
  N11: GPIO.GPIO12, Phi.SLEEP
  N12: GPIO.GPIO24, Theta.M0
  N13: GPIO.GPIO23, Theta.M1
  N14: GPIO.GPIO18, Theta.DIRECTION
  N15: Theta.VMOT, Phi.VMOT, C1.+, C2.+, 5V_8A.VCC
  N16: Theta.GND#141, Phi.GND#141, C1.-, C2.-, 5V_8A.GND
  N17: Theta.2B, J5.pin1, THETA.pin1
  N18: Theta.2A, J5.pin2, THETA.pin2
  N19: Theta.1A, J5.pin3, THETA.pin3
  N20: Theta.1B, J5.pin4, THETA.pin4
  N21: Theta.FAULT, R3.Pin_1
  N22: Phi.2B, J6.pin1
  N23: Phi.2A, J6.pin2
  N24: Phi.1A, J6.pin3
  N25: Phi.1B, J6.pin4
  N26: Phi.FAULT, R2.Pin_1
  N27: Phi.GND#147, R3.Pin_0, led_4.anode, led_3.cathode
  N28: M3.A, J3.pin4
  N29: M3.C, J3.pin3
  N30: M3.B, J3.pin2
  N31: M3.D, J3.pin1
  N32: R2.Pin_0, led_3.anode
  N33: M4.A, J4.pin4
  N34: M4.C, J4.pin3
  N35: M4.B, J4.pin2
  N36: M4.D, J4.pin1
  N37: Shutter1.anode, S_opto.Pin_2
  N38: Focus1.anode, F_opto.Pin_2
  N39: F_opto.Pin_4, S_opto.Pin_4, Trigger_Connector.pin2
  N40: F_opto.Pin_3, Trigger_Connector.pin3
  N41: S_opto.Pin_3, Trigger_Connector.pin1
  N42: Alerts2.cathode, R6.Pin_1

custom parts:
  DRV8834 Low-Voltage Stepper Motor Driver Carrier: This is a breakout board for TI’s DRV8834 microstepping bipolar stepper motor driver. It has a pinout and interface that are nearly identical to those of our A4988 carriers, so it can be used as a drop-in replacement for those boards in many applications. The DRV8834 operates from 2.5–10.8 V, allowing stepper motors to be powered with voltages that are too low for other drivers, and can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
